# Fritzing sketch solar_heating_control_breadboard (saved by Fritzing 0.9.2b)
circuit board: 8.46667cm x 5.64444cm
breadboards: 1

parts:
  Part1 = Arduino Yun
  LED1 = LED - 5mm [color="Red (633nm)" package="5 mm [THT]"]
  R1 = Resistor [tolerance=±5% resistance=220 package=THT]
  DS1 = DS18B20 1-Wire Temperature Sensor [part_number=DS18B20]
  R2 = Resistor [tolerance=±5% resistance=4.7k package=THT]
  DS2 = DS18B20 1-Wire Temperature Sensor [part_number=DS18B20]
  R3 = Resistor [tolerance=±5% resistance=10k package=THT]
  U1 = TLP621 [part_number="Get Impulse from Wattmeter" package=THT]
  U2 = RELAY [package=relay-jzc]

nets:
  VDD: Part1.5V, DS1.VDD, R2.Pin_0, DS2.VDD, R3.Pin_0
  N1: Part1.D10_PWM/SS, DS1.DQ, R2.Pin_1, DS2.DQ
  N2: Part1.D12/MISO, R1.Pin_0
  GND: Part1.GND, LED1.cathode, DS1.GND, DS2.GND, U1.Pin_3, U2.COIL1
  N3: Part1.D2, R3.Pin_1, U1.Pin_4
  N4: LED1.anode, R1.Pin_1, U2.MAIN
