# Fritzing sketch solar_heating_control_protoshield (saved by Fritzing 0.9.2b)

parts:
  LED1 = LED - 5mm [color="Red (633nm)" package="5 mm [THT]"]
  U1 = RELAY [package=relay-jzc]
  DS1 = DS18B20 1-Wire Temperature Sensor [part_number=DS18B20]
  DS2 = DS18B20 1-Wire Temperature Sensor [part_number=DS18B20]
  R1 = Resistor [tolerance=±5% resistance=220 package=THT]
  R2 = Resistor [tolerance=±5% resistance=10k package=THT]
  R3 = Resistor [tolerance=±5% resistance=4.7k package=THT]
  Part2 = Arduino Prototyping Shield
  U2 = TLP621 [part_number="Get Impulse from Wattmeter" package=THT]
  Part1 = Arduino Yun  # not connected

nets:
  GND: LED1.cathode, U1.MAIN, DS1.GND, DS2.GND, Part2.GND, Part2.N$62, Part2.N$77, Part2.N$108, U2.Pin_3
  N1: LED1.anode, U1.COIL1, R1.Pin_0, Part2.N$96
  VDD: DS1.VDD, DS2.VDD, R2.Pin_0, R3.Pin_0, Part2.+5V, Part2.N$37, Part2.N$72, Part2.N$178, Part2.N$376
  N2: DS1.DQ, Part2.D10, Part2.N$48, Part2.N$49
  N3: DS2.DQ, R3.Pin_1, Part2.N$79, Part2.N$86
  N4: R1.Pin_1, Part2.D12, Part2.N$245
  N5: R2.Pin_1, Part2.D2, Part2.N$81, U2.Pin_4
